# Fritzing sketch ir_receiver (saved by Fritzing 0.9.3b)
breadboards: 1

parts:
  パーツ1 = Arduino Uno (Rev3)
  パーツ2 = Infra red receiver

nets:
  N1: パーツ1.D11_PWM/MOSI, パーツ2.Data
  5V: パーツ1.5V, パーツ2.VCC
  GND: パーツ1.GND, パーツ2.GND
